# Fritzing sketch electronics (saved by Fritzing 0.9.10b)

parts:
  U1 = ESP8266 ESP-01 Upgraded WiFi Module [part_number=ESP8266]
  Part1 = NeoPixel Stick [part_number=1426]
  MP1584EN_Board1 = MP1584EN Power Regulator Board [part_number=MP1584EN]
  V1 = DC Power [voltage=5]

nets:
  VCC: U1.VCC, Part1.+5V, MP1584EN_Board1.OUT_+
  N1: U1.GPIO_2, Part1.DATAIN
  GND: U1.GND, Part1.GND, MP1584EN_Board1.OUT_-
  N2: MP1584EN_Board1.IN_-, V1.V-
  N3: MP1584EN_Board1.IN_+, V1.V+

custom parts:
  ESP8266 ESP-01 Upgraded WiFi Module: Upgraded Version ESP-01,all Flash are upgraded to 1M byte.Also support Cloud service remote transmission.
  NeoPixel Stick: Make your own little LED strip arrangement with this stick of NeoPixel LEDs. We crammed 8 of the tiny 5050 (5mm x 5mm) smart RGB LEDs onto a PCB with mounting holes and a chainable design. Use only one microcontroller pin to control as many as you can chain together! Each LED is addressable as the driver chip is inside the LED. Each one has ~18mA constant current drive so the color will be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
  MP1584EN Power Regulator Board: The MP1584EN is a high frequency step-down switching regulator. The input voltage range is 4.5V to 28V. The output voltage is set by the board's potentiometer.
